# Fritzing sketch DartShooterBuild (saved by Fritzing 0.9.10b)
breadboards: 3

parts:
  Part1 = Arduino Nano (Rev3.0) (ICSP)
  U1 = MAX7219 [package=dil24]
  12v_Solenoid = Solenoid
  12v_Desktop_Power_Supply1 = LIPO-2000mAh [package=lipo-2000]
  5V_Relay = 1 chan 5v relay module
  7_4_Volts_(_SERVO_) = RioRand LM2596
  5V_(_ARDUINO_&_DISPLAY_) = RioRand LM2596
  J1 = Basic Servo
  C1 = Capacitor [package=cap-pth-small2]
  C2 = Capacitor Polarized [package=cpol-radial-100uf-25v]
  R1 = Resistor [tolerance=±5% resistance=330 package="0402 [SMD]"]
  J5 = Camdenboss CTB0158-2 [part_number=CTB0158-2 package=THT]
  J6 = Camdenboss CTB0158-2 [part_number=CTB0158-2 package=THT]
  R2 = Resistor [tolerance=±5% resistance=1k package="0402 [SMD]"]
  C3 = Capacitor [package=cap-pth-small2]
  C4 = Capacitor [package=cap-pth-small2]
  R3 = Resistor [tolerance=±5% resistance=1k package="0402 [SMD]"]
  C5 = Capacitor [package=cap-pth-small2]
  R4 = Resistor [tolerance=±5% resistance=1k package="0402 [SMD]"]
  J7 = Camdenboss CTB0158-4 [part_number=CTB0158-4 package=THT]
  J8 = Camdenboss CTB0158-4 [part_number=CTB0158-4 package=THT]
  J9 = Camdenboss CTB0158-4 [part_number=CTB0158-4 package=THT]
  J10 = Camdenboss CTB0158-6 [part_number=CTB0158-6 package=THT]
  Counter_Clockwise = Round Pushbutton
  Clockwise = Round Pushbutton
  Clear = Round Pushbutton
  Launch_Counter = 7-Segment-Display-3-Red [part_number=HS320561K package="7-Segment-3 [THT]"]
  J11 = Camdenboss CTB0158-4 [part_number=CTB0158-4 package=THT]
  J12 = Camdenboss CTB0158-4 [part_number=CTB0158-4 package=THT]
  J13 = Camdenboss CTB0158-2 [part_number=CTB0158-2 package=THT]
  FIRE = Round Pushbutton
  R5 = Resistor [tolerance=±5% resistance=220 package="0402 [SMD]"]
  R6 = Resistor [tolerance=±5% resistance=220 package="0402 [SMD]"]
  R7 = Resistor [tolerance=±5% resistance=220 package="0402 [SMD]"]
  R8 = Resistor [tolerance=±5% resistance=220 package="0402 [SMD]"]
  Flyback_Diode = Diode [package=diode-hv]
  Illuminated_Safety_Toggle = Taiway 100-SP-X-T1 SPDT Miniature Toggle Switch [part_number=100-SP-X-T1-0-0-B1-M1 package=THT]

nets:
  GND: Part1.GND, 7_4_Volts_(_SERVO_).Pin_4, J1.gnd, J6.pin1, J7.pin4, J11.pin2, R6.Pin_1, R7.Pin_1, R8.Pin_1
  N1: Part1.D2, J7.pin1
  N2: Part1.D3, J7.pin2
  N3: Part1.D4, J7.pin3
  N4: Part1.D5, J11.pin1
  N5: Part1.D6, J12.pin1, R8.Pin_0
  N6: Part1.D7, J12.pin2, R7.Pin_0
  N7: Part1.D8, J12.pin3, R6.Pin_0
  N8: Part1.D9, J11.pin4
  N9: Part1.VIN, J6.pin2
  N10: Part1.5V, J11.pin3, J12.pin4, J13.pin1, R5.Pin_0
  N11: Part1.D13/SCK, J13.pin2, R5.Pin_1
  N12: U1.DIN, R2.Pin_1
  N13: U1.DIG0, J10.pin1
  GND_2: U1.GND, U1.GND2, U1.SEGA, U1.SEGB, C1.2, C2.-, J5.pin1, R2.Pin_0, C3.1, C4.1, R3.Pin_0, C5.1, R4.Pin_0, J8.pin1, J10.pin2, J10.pin6
  N14: U1.DIG2, J10.pin5
  N15: U1.DIG1, J10.pin4
  N16: U1.LOAD, R3.Pin_1
  N17: U1.CLK, R4.Pin_1
  N18: U1.SEGF, J10.pin3
  N19: U1.SEGG, J9.pin4
  N20: U1.ISET, R1.Pin_1
  N21: U1.VCC, C1.1, C2.+, R1.Pin_0, J5.pin2
  N22: U1.SEGC, J9.pin3
  N23: U1.SEGE, J9.pin1
  N24: U1.SEGD, J9.pin2
  N25: 12v_Solenoid.pin1, 7_4_Volts_(_SERVO_).Pin_2, 5V_(_ARDUINO_&_DISPLAY_).Pin_2, Flyback_Diode.A
  N26: 12v_Solenoid.pin2, 5V_Relay.pin_4, Flyback_Diode.C
  N27: 12v_Desktop_Power_Supply1.+, Illuminated_Safety_Toggle.L2
  N28: 12v_Desktop_Power_Supply1.-, Illuminated_Safety_Toggle.COM
  N29: 5V_Relay.pin_1, J11.terminal_3
  N30: 5V_Relay.pin_2, J11.terminal_2
  N31: 5V_Relay.pin_3, J11.terminal_1
  N32: 5V_Relay.pin_5, 7_4_Volts_(_SERVO_).Pin_1, 5V_(_ARDUINO_&_DISPLAY_).Pin_1, Illuminated_Safety_Toggle.L1
  N33: 7_4_Volts_(_SERVO_).Pin_3, J1.vcc
  N34: 5V_(_ARDUINO_&_DISPLAY_).Pin_3, J5.terminal_2, J6.terminal_2
  N35: 5V_(_ARDUINO_&_DISPLAY_).Pin_4, J5.terminal_1, J6.terminal_1
  N36: J1.pulse, J11.terminal_4
  N37: C3.2, J8.pin3
  N38: C4.2, J8.pin2
  N39: C5.2, J8.pin4
  N40: J7.terminal_1, J8.terminal_4
  N41: J7.terminal_2, J8.terminal_3
  N42: J7.terminal_3, J8.terminal_2
  N43: J7.terminal_4, J8.terminal_1
  N44: J9.terminal_1, Launch_Counter.pin1
  N45: J9.terminal_2, Launch_Counter.pin2
  N46: J9.terminal_3, Launch_Counter.pin4
  N47: J9.terminal_4, Launch_Counter.pin5
  N48: J10.terminal_1, Launch_Counter.pin_12
  N49: J10.terminal_2, Launch_Counter.pin_11
  N50: J10.terminal_3, Launch_Counter.pin_10
  N51: J10.terminal_4, Launch_Counter.pin_9
  N52: J10.terminal_5, Launch_Counter.pin8
  N53: J10.terminal_6, Launch_Counter.pin7
  N54: Counter_Clockwise.leg0, J12.terminal_3
  N55: Counter_Clockwise.leg1, Clockwise.leg1, Clear.leg1, J12.terminal_4
  N56: Clockwise.leg0, J12.terminal_2
  N57: Clear.leg0, J12.terminal_1
  N58: J13.terminal_1, FIRE.leg0
  N59: J13.terminal_2, FIRE.leg1

custom parts:
  1 chan 5v relay module: 1 Channel 5V Relay Module Board Shield with Optocoupler Support High and Low Level Trigger for Arduino.
  7-Segment-Display-3-Red: 7-Segment Display 3 digits Red
