# Fritzing sketch dart_launcher_diagram (saved by Fritzing 0.9.10b)
breadboards: 1

parts:
  RESET = Pushbutton [package="[THT]"]  # not connected
  SHOOT = Pushbutton [package="[THT]"]  # not connected
  U1 = LIPO-2000mAh [package=lipo-2000]
  L1 = Solenoid
  part = Arduino Nano (Rev3.0) (ICSP)
  12v_->_7_4v = DC_DC_XL4016 [package=board_screw]
  VCC1 = Battery block 9V  # not connected
  Solenoid_Kill_Switch = Toggle Switch [package=THT]
  M1 = 1-chan-5v-relay-module_1
  SERVO_MOTOR = Basic Servo
  Solenoid_Relay = Camdenboss CTB0158-3 [part_number=CTB0158-3 package=THT]
  SHOOT_2 = Camdenboss CTB0158-2 [part_number=CTB0158-2 package=THT]
  RESET_2 = Camdenboss CTB0158-2 [part_number=CTB0158-2 package=THT]
  9V_Power = Camdenboss CTB0158-2 [part_number=CTB0158-2 package=THT]
  SERVO = Camdenboss CTB0158-3 [part_number=CTB0158-3 package=THT]
  SHIFT_REGISTER = 74HC595 [package="DIP16 [THT]"]
  R11 = Resistor [tolerance=±5% power=0.25 resistance=220 package=THT]
  R12 = Resistor [tolerance=±5% power=0.25 resistance=220 package=THT]
  R13 = Resistor [tolerance=±5% power=0.25 resistance=220 package=THT]
  R14 = Resistor [tolerance=±5% power=0.25 resistance=220 package=THT]
  R15 = Resistor [tolerance=±5% power=0.25 resistance=220 package=THT]
  R16 = Resistor [tolerance=±5% power=0.25 resistance=220 package=THT]
  R17 = Resistor [tolerance=±5% power=0.25 resistance=220 package=THT]
  R18 = Resistor [tolerance=±5% power=0.25 resistance=220 package=THT]
  R19 = Resistor [tolerance=±5% power=0.25 resistance=220 package=THT]
  R20 = Resistor [tolerance=±5% power=0.25 resistance=220 package=THT]
  U2 = 7-SEGMENT-4DIGIT [package=7-segment-4digit-youngsun]  # not connected

nets:
  N1: U1.+, Solenoid_Kill_Switch.COM
  N2: U1.-, L1.pin1, 12v_->_7_4v.IN-
  N3: L1.pin2, M1.connector3
  GND: part.GND, Solenoid_Relay.pin2, 9V_Power.pin1, SERVO.pin1, SERVO.pin3, SHIFT_REGISTER.GND, SHIFT_REGISTER.OE, R11.Pin_0, R12.Pin_0
  N4: part.D2, SHIFT_REGISTER.SH_CP
  N5: part.D3, SHIFT_REGISTER.ST_CP
  N6: part.D4, SHIFT_REGISTER.DS
  N7: part.D5, RESET_2.pin1, R12.Pin_1
  N8: part.D6, SHOOT_2.pin1, R11.Pin_1
  N9: part.D7, SERVO.pin2
  N10: part.D9, Solenoid_Relay.pin3
  VIN: part.VIN, Solenoid_Relay.pin1, SHOOT_2.pin2, RESET_2.pin2, 9V_Power.pin2, SHIFT_REGISTER.MR, SHIFT_REGISTER.VCC
  N11: 12v_->_7_4v.IN+, Solenoid_Kill_Switch.L2, M1.connector4
  N12: 12v_->_7_4v.OUT+, SERVO_MOTOR.vcc
  N13: SHIFT_REGISTER.Q1, R18.Pin_1
  N14: SHIFT_REGISTER.Q2, R14.Pin_1
  N15: SHIFT_REGISTER.Q3, R19.Pin_1
  N16: SHIFT_REGISTER.Q4, R15.Pin_1
  N17: SHIFT_REGISTER.Q5, R20.Pin_1
  N18: SHIFT_REGISTER.Q6, R16.Pin_1
  N19: SHIFT_REGISTER.Q7, R17.Pin_1
  N20: SHIFT_REGISTER.Q0, R13.Pin_0
