# Fritzing sketch dart_launcher_pcb (saved by Fritzing 0.9.10b)
breadboards: 1

parts:
  part = Arduino Nano (Rev3.0) (ICSP)
  Solenoid_Relay = Camdenboss CTB0158-3 [part_number=CTB0158-3 package=THT]
  SHOOT = Camdenboss CTB0158-2 [part_number=CTB0158-2 package=THT]
  RESET = Camdenboss CTB0158-2 [part_number=CTB0158-2 package=THT]
  9V_Power = Camdenboss CTB0158-2 [part_number=CTB0158-2 package=THT]
  SERVO = Camdenboss CTB0158-3 [part_number=CTB0158-3 package=THT]
  SHIFT_REGISTER = 74HC595 [package="DIP16 [THT]"]
  R11 = Resistor [tolerance=±5% power=0.25 resistance=220 package=THT]
  R12 = Resistor [tolerance=±5% power=0.25 resistance=220 package=THT]
  R13 = Resistor [tolerance=±5% power=0.25 resistance=220 package=THT]
  R14 = Resistor [tolerance=±5% power=0.25 resistance=220 package=THT]
  R15 = Resistor [tolerance=±5% power=0.25 resistance=220 package=THT]
  R16 = Resistor [tolerance=±5% power=0.25 resistance=220 package=THT]
  R17 = Resistor [tolerance=±5% power=0.25 resistance=220 package=THT]
  R18 = Resistor [tolerance=±5% power=0.25 resistance=220 package=THT]
  R19 = Resistor [tolerance=±5% power=0.25 resistance=220 package=THT]
  R20 = Resistor [tolerance=±5% power=0.25 resistance=220 package=THT]
  U2 = 7-SEGMENT-4DIGIT [package=7-segment-4digit-youngsun]  # not connected

nets:
  GND: part.GND, Solenoid_Relay.pin2, 9V_Power.pin1, SERVO.pin1, SERVO.pin3, SHIFT_REGISTER.GND, SHIFT_REGISTER.OE, R11.Pin_0, R12.Pin_0
  N1: part.D2, SHIFT_REGISTER.SH_CP
  N2: part.D3, SHIFT_REGISTER.ST_CP
  N3: part.D4, SHIFT_REGISTER.DS
  N4: part.D5, RESET.pin1, R12.Pin_1
  N5: part.D6, SHOOT.pin1, R11.Pin_1
  N6: part.D7, SERVO.pin2
  N7: part.D9, Solenoid_Relay.pin3
  VIN: part.VIN, Solenoid_Relay.pin1, SHOOT.pin2, RESET.pin2, 9V_Power.pin2, SHIFT_REGISTER.MR, SHIFT_REGISTER.VCC
  N8: SHIFT_REGISTER.Q1, R18.Pin_1
  N9: SHIFT_REGISTER.Q2, R14.Pin_1
  N10: SHIFT_REGISTER.Q3, R19.Pin_1
  N11: SHIFT_REGISTER.Q4, R15.Pin_1
  N12: SHIFT_REGISTER.Q5, R20.Pin_1
  N13: SHIFT_REGISTER.Q6, R16.Pin_1
  N14: SHIFT_REGISTER.Q7, R17.Pin_1
  N15: SHIFT_REGISTER.Q0, R13.Pin_0
