# Fritzing sketch dart_launcher_prototype (saved by Fritzing 0.9.10b)
breadboards: 1

parts:
  RESET = Pushbutton [package="[THT]"]
  SHOOT = Pushbutton [package="[THT]"]
  12v_Power_Supply = LIPO-2000mAh [package=lipo-2000]
  12v_Solenoid = Solenoid
  Part1 = Arduino Nano (Rev3.0) (ICSP)
  12v_->_7_4v_Buck_Converter = DC_DC_XL4016 [package=board_screw]
  VCC1 = Battery block 9V
  12v_Power_Kill_Switch = Toggle Switch [package=THT]
  MG995 = Basic Servo
  Solenoid_Relay = Camdenboss CTB0158-3 [part_number=CTB0158-3 package=THT]
  SHOOT_2 = Camdenboss CTB0158-2 [part_number=CTB0158-2 package=THT]
  RESET_2 = Camdenboss CTB0158-2 [part_number=CTB0158-2 package=THT]
  9V_Power = Camdenboss CTB0158-2 [part_number=CTB0158-2 package=THT]
  SERVO = Camdenboss CTB0158-3 [part_number=CTB0158-3 package=THT]
  SHIFT_REGISTER = 74HC595 [package="DIP16 [THT]"]
  R11 = Resistor [tolerance=±5% power=0.25 resistance=220 package=THT]
  R12 = Resistor [tolerance=±5% power=0.25 resistance=220 package=THT]
  R13 = Resistor [tolerance=±5% power=0.25 resistance=220 package=THT]
  R14 = Resistor [tolerance=±5% power=0.25 resistance=220 package=THT]
  R15 = Resistor [tolerance=±5% power=0.25 resistance=220 package=THT]
  R16 = Resistor [tolerance=±5% power=0.25 resistance=220 package=THT]
  R17 = Resistor [tolerance=±5% power=0.25 resistance=220 package=THT]
  R18 = Resistor [tolerance=±5% power=0.25 resistance=220 package=THT]
  R19 = Resistor [tolerance=±5% power=0.25 resistance=220 package=THT]
  R20 = Resistor [tolerance=±5% power=0.25 resistance=220 package=THT]
  5V_Relay = 1 chan 5v relay module
  UP = Pushbutton [package="[THT]"]
  RESET2 = Camdenboss CTB0158-2 [part_number=CTB0158-2 package=THT]
  DOWN = Pushbutton [package="[THT]"]
  RESET4 = Camdenboss CTB0158-2 [part_number=CTB0158-2 package=THT]
  R21 = Resistor [tolerance=±5% power=0.25 resistance=220 package=THT]
  R22 = Resistor [tolerance=±5% power=0.25 resistance=220 package=THT]
  TODO_Wire_To_595 = 7-Segment-Display-3-Red [part_number=HS320561K package="7-Segment-3 [THT]"]  # not connected

nets:
  N1: RESET.Pin_1, RESET.Pin_2, RESET_2.terminal_1
  N2: RESET.Pin_3, RESET.Pin_4, RESET_2.terminal_2
  N3: SHOOT.Pin_1, SHOOT.Pin_2, SHOOT_2.terminal_1
  N4: SHOOT.Pin_3, SHOOT.Pin_4, SHOOT_2.terminal_2
  N5: 12v_Power_Supply.+, 12v_Power_Kill_Switch.COM
  N6: 12v_Power_Supply.-, 12v_Solenoid.pin1, 12v_->_7_4v_Buck_Converter.IN-
  N7: 12v_Solenoid.pin2, 5V_Relay.pin_4
  GND: Part1.GND, 12v_->_7_4v_Buck_Converter.OUT-, VCC1.-, VCC1.+, Solenoid_Relay.pin2, 9V_Power.pin1, SERVO.pin3, SHIFT_REGISTER.GND, SHIFT_REGISTER.OE, R11.Pin_0, R12.Pin_0, R21.Pin_0, R22.Pin_0
  N8: Part1.D2, SHIFT_REGISTER.SH_CP
  N9: Part1.D3, SHIFT_REGISTER.ST_CP
  N10: Part1.D4, SHIFT_REGISTER.DS
  N11: Part1.D5, RESET_2.pin1, R12.Pin_1
  N12: Part1.D6, SHOOT_2.pin1, R11.Pin_1
  N13: Part1.D7, SERVO.pin2
  N14: Part1.D9, Solenoid_Relay.pin3
  N15: Part1.D10, RESET2.pin1, R22.Pin_1
  N16: Part1.D11/MOSI, RESET4.pin1, R21.Pin_1
  VIN: Part1.VIN, Solenoid_Relay.pin1, SHOOT_2.pin2, RESET_2.pin2, 9V_Power.pin2, SHIFT_REGISTER.MR, SHIFT_REGISTER.VCC, RESET2.pin2, RESET4.pin2
  N17: 12v_->_7_4v_Buck_Converter.IN+, 12v_Power_Kill_Switch.L2, 5V_Relay.pin_5
  N18: 12v_->_7_4v_Buck_Converter.OUT+, SERVO.pin1
  N19: MG995.gnd, SERVO.terminal_3
  N20: MG995.vcc, SERVO.terminal_1
  N21: MG995.pulse, SERVO.terminal_2
  N22: Solenoid_Relay.terminal_1, 5V_Relay.pin_1
  N23: Solenoid_Relay.terminal_2, 5V_Relay.pin_2
  N24: Solenoid_Relay.terminal_3, 5V_Relay.pin_3
  N25: SHIFT_REGISTER.Q1, R18.Pin_1
  N26: SHIFT_REGISTER.Q2, R14.Pin_1
  N27: SHIFT_REGISTER.Q3, R19.Pin_1
  N28: SHIFT_REGISTER.Q4, R15.Pin_1
  N29: SHIFT_REGISTER.Q5, R20.Pin_1
  N30: SHIFT_REGISTER.Q6, R16.Pin_1
  N31: SHIFT_REGISTER.Q7, R17.Pin_1
  N32: SHIFT_REGISTER.Q0, R13.Pin_0
  N33: UP.Pin_1, UP.Pin_2, RESET2.terminal_1
  N34: UP.Pin_3, UP.Pin_4, RESET2.terminal_2
  N35: DOWN.Pin_1, DOWN.Pin_2, RESET4.terminal_1
  N36: DOWN.Pin_3, DOWN.Pin_4, RESET4.terminal_2

custom parts:
  1 chan 5v relay module: 1 Channel 5V Relay Module Board Shield with Optocoupler Support High and Low Level Trigger for Arduino.
  7-Segment-Display-3-Red: 7-Segment Display 3 digits Red
